# Fritzing sketch ESP8266_FLASHBOARD (saved by Fritzing 0.9.3b)

parts:
  ESP8266-2 = ESP8266-12 [part_number=ESP8266-12]  # not connected
  S2 = Toggle Switch [package=THT]
  J11 = female pin header, 2 pins [form="♀ (female)"]  # not connected
  J12 = female pin header, 2 pins [form="♀ (female)"]
  J13 = female pin header, 2 pins [form="♀ (female)"]
  J14 = female pin header, 2 pins [form="♀ (female)"]  # not connected
  J15 = female pin header, 2 pins [form="♀ (female)"]  # not connected
  J16 = female pin header, 2 pins [form="♀ (female)"]
  J17 = female pin header, 2 pins [form="♀ (female)"]
  J18 = female pin header, 2 pins [form="♀ (female)"]
  M4 = CH340

nets:
  N1: S2.L1, M4.connector7
  N2: S2.COM, J16.pin1, J17.pin2
  N3: J12.pin1, J12.pin2, J13.pin1, M4.connector4
  N4: J18.pin1, M4.connector5
  N5: J18.pin2, M4.connector6
