# Fritzing sketch ESP8266_PN532_RGB_LED_ (saved by Fritzing 0.9.3b)

parts:
  ESP8266-1 = ESP8266-12 [part_number=ESP8266-12]
  Bauteil1 = PN532 Elechouse RFID NFC Module V3
  LED1 = RGB LED PL9823 F5 [package="5 mm [THT]"]
  LED3 = LED - 3mm [color="Red (633nm)" package="3 mm [THT]"]
  J1 = Screw terminal - 2 pins [package=THT]

nets:
  N1: ESP8266-1.GPIO14, LED1.VDD
  N2: ESP8266-1.GPIO12, LED1.DIN
  N3: ESP8266-1.GPIO13, LED1.DO
  VCC: ESP8266-1.VCC, Bauteil1.VCC, J1.pin2
  N4: ESP8266-1.RXD, LED3.anode
  N5: ESP8266-1.GPIO4, Bauteil1.SDA
  N6: ESP8266-1.GPIO5, Bauteil1.SCL
  GND: ESP8266-1.GND, Bauteil1.GND, LED1.GND, LED3.cathode, J1.pin1

notes:
  3.3V
  DIP switches to HSU

custom parts:
  PN532 Elechouse RFID NFC Module V3: NFC is a popular technology in recent years. We often heard this work while smart phone company such as Samsung or HTC introduces their latest high-end phones. Almost all the high-end phone in the market support NFC. Near field communication (NFC) is a set of standards for smart phones and similar devices to establish radio communication with each other by touching them together or bringing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
  RGB LED PL9823 F5: A 5mm tri-color LED with red, green and blue inside. this led includes WS2811 controller.
